// Digital circuit signal generator and character indexer.dig as structural Verilog
module signal_generator_and_character_indexer (
  input  pxl,
  input  pxl_2
);

  wire _74161_1_pin1, _74161_1_pin15, _74161_2_pin15, _74161_4_pin1, _74161_4_pin2, _74161_4_pin15, undriven;
  wire [7:0] img_d;
  wire [15:0] _74161_1_pin14;

  _74161 _74161_1 (
    .pin1(_74161_1_pin1), .pin2(pxl), .pin3(1'b0), .pin4(1'b0), .pin5(1'b0), .pin6(1'b0), .pin7(1'b1),
    .pin8(1'b0), .pin9(1'b1), .pin10(1'b1), .pin11(_74161_1_pin14[3]), .pin12(_74161_1_pin14[2]),
    .pin13(_74161_1_pin14[1]), .pin14(_74161_1_pin14[0]), .pin15(_74161_1_pin15), .pin16(1'b1));
  _74161 _74161_2 (
    .pin1(_74161_1_pin1), .pin2(pxl), .pin3(1'b0), .pin4(1'b0), .pin5(1'b0), .pin6(1'b0), .pin7(1'b1),
    .pin8(1'b0), .pin9(1'b1), .pin10(_74161_1_pin15), .pin11(_74161_1_pin14[7]), .pin12(_74161_1_pin14[6]),
    .pin13(_74161_1_pin14[5]), .pin14(_74161_1_pin14[4]), .pin15(_74161_2_pin15), .pin16(1'b1));
  _74161 _74161_3 (
    .pin1(_74161_1_pin1), .pin2(pxl), .pin3(1'b0), .pin4(1'b0), .pin5(1'b0), .pin6(1'b0), .pin7(1'b1),
    .pin8(1'b0), .pin9(1'b1), .pin10(_74161_2_pin15), .pin16(1'b1));  // open: pin11, pin12, pin13, pin14, pin15
  _74161 _74161_4 (
    .pin1(_74161_4_pin1), .pin2(_74161_4_pin2), .pin3(1'b0), .pin4(1'b0), .pin5(1'b0), .pin6(1'b0),
    .pin7(1'b1), .pin8(1'b0), .pin9(1'b1), .pin10(1'b1), .pin11(_74161_1_pin14[11]),
    .pin12(_74161_1_pin14[10]), .pin13(_74161_1_pin14[9]), .pin14(_74161_1_pin14[8]), .pin15(_74161_4_pin15),
    .pin16(1'b1));
  _74161 _74161_5 (
    .pin1(_74161_4_pin1), .pin2(_74161_4_pin2), .pin3(1'b0), .pin4(1'b0), .pin5(1'b0), .pin6(1'b0),
    .pin7(1'b1), .pin8(1'b0), .pin9(1'b1), .pin10(_74161_4_pin15), .pin11(_74161_1_pin14[15]),
    .pin12(_74161_1_pin14[14]), .pin13(_74161_1_pin14[13]), .pin14(_74161_1_pin14[12]), .pin16(1'b1));  // open: pin15
  ROM #(.AddrBits(16), .isProgramMemory("true"), .Bits(8)) img (.A(_74161_1_pin14), .sel(1'b1), .D(img_d));
  VGA vga_1 (.R(img_d[7:5]), .G(img_d[4:2]), .B({img_d[1:0], 1'b1}), .H(1'b0), .V(undriven), .C(pxl_2));

  // Notes on the sheet:
  //   pxl: Hz: 500
  //   pxl_2: Hz: 2000
  //   Pulses on frame end
  //   Column counter
  //   Line counter
  //   Pixel coord
  //   bus
  //   !(BC)
  //   !(ADEFH) - !vVisS
  //   !(AD)
  //   !(ADE) - !vSyncS
  //   !(AF) - !hVisS
  //   !(BCEH) - !hSyncR
  //   !(BCF) - !hVisR
  //   !(BCDEI) - !hSyncS
  //   !(ADFG)  - !vVisR/!vSyncR
  //   contents of img (hex, n*v repeats v):
  //   256*ff,8*e0,8*1c,8*e0,8*1c,8*e0,8*1c,8*e0,8*1c,8*e0,8*1c,8*e0
  //   ,8*1c,8*e0,8*1c,8*e0,8*1c,8*e0,8*1c,8*e0,8*1c,8*e0,8*1c,8*e0,8*1c
  //   ,8*e0,8*1c,8*e0,8*1c,8*e0,8*1c,8*e0,8*1c,8*ff,8*0,232*ff
endmodule
